# Fritzing sketch BikeTrainer (saved by Fritzing 0.9.3b)
circuit board: 8.46667cm x 5.64444cm
breadboards: 1

parts:
  R1 = Resistor [tolerance=±5% resistance=220 package=THT]
  R2 = Resistor [tolerance=±5% resistance=220 package=THT]
  S1 = Reed switch [package=THT]
  S2 = Reed switch [package=THT]
  Componente1 = Arduino Uno (Rev3)

nets:
  N1: R1.Pin_0, S2.pin_1, Componente1.A1
  N2: R1.Pin_1, R2.Pin_0, Componente1.GND
  N3: R2.Pin_1, S1.pin_2, Componente1.A0
  N4: S1.pin_1, S2.pin_2, Componente1.5V

// code stored in the sketch: BikeTrainer.ino

